# Fritzing sketch Pico (saved by Fritzing 1.0.3b)

parts:
  Part1 = Adafruit MAX98357A I2S 3W Class D Amplifier [part_number="Adafruit #3006"]
  Mod2 = Raspberry Pi Pico
  A1 = bone conduction transducer

nets:
  N1: Part1.VIN, Mod2.pin_36
  N2: Part1.DIN, Mod2.pin_5
  N3: Part1.BCLK, Mod2.pin_1
  N4: Part1.LRCLK, Mod2.pin_2
  N5: Part1.VO-, A1.Pin_1
  N6: Part1.VO+, A1.Pin_2

custom parts:
  Adafruit MAX98357A I2S 3W Class D Amplifier: Listen to this good news - we now have an all in one digital audio amp breakout board that works incredibly well with the Raspberry Pi! If you're looking for an easy and low cost way to get you digital sound files bumpin' then the MAX08357 I2S Amp Breakout is for you. It takes standard I2S digital audio input and, not only decodes it into analog, but also amplifies it directly into a speaker.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
  Raspberry Pi Pico: Raspberry Pi Pico. Based around the RP2040 microcontroller the Pico is a low cost microcontroller device bringing Raspberry Pi quality, cost, and easy of use to the microcontroller space. Jan 2021, Split part in to two versions: tht (this one) and SMD. This one will drill holes for a .1 in header in pcb to allow plugging in the module as well as providing pads to solder the module to the top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
  bone conduction transducer: Bone Conductor Transducer with Wires - 8 Ohm 1 Watt.
